# Fritzing sketch XmasBlinky (saved by Fritzing 0.9.3b)
breadboards: 1

parts:
  Raspberry_Pi_1 = Raspberry Pi 3 [part_number=RPI-3-V1.2]
  R1 = Resistor [tolerance=±5% resistance=560 package=THT]
  LED1 = LED - 5mm [color="Red (633nm)" package="5 mm [THT]"]
  LED2 = LED - 5mm [color="Green (565nm)" package="5 mm [THT]"]
  R2 = Resistor [tolerance=±5% resistance=560 package=THT]
  MCP3009 = IC, DIP package, 16 pins [chip_label=MCP3008 part_number=MCP3008]
  R3 = Resistor [tolerance=±5% resistance=560 package=THT]
  R4 = Photocell (LDR) [package=THT]
  SPKR1 = Loudspeaker  # not connected

nets:
  N1: Raspberry_Pi_1.3v3, R1.Pin_0, R2.Pin_0, MCP3009.pin15, MCP3009.pin16, R4.pin_0
  N2: Raspberry_Pi_1.GPIO9, MCP3009.pin11
  N3: Raspberry_Pi_1.GPIO11, MCP3009.pin12
  N4: Raspberry_Pi_1.GND, MCP3009.pin9, MCP3009.pin13, MCP3009.pin14, R3.Pin_0
  N5: Raspberry_Pi_1.GPIO5, LED1.anode
  N6: Raspberry_Pi_1.GPIO6, LED2.anode
  N7: Raspberry_Pi_1.GPIO7, MCP3009.pin10
  N8: R1.Pin_1, LED1.cathode
  N9: LED2.cathode, R2.Pin_1
  N10: MCP3009.pin3, R3.Pin_1, R4.pin_1
